// Digital circuit 1 aula.dig as structural Verilog
module _1_aula (
);

  wire ch1_b, ch2_b, ch3_b, ch4_b, k1_p3, k3_p5, relaydt_1_p4;

  Switch ch3 (.A(1'b1), .B(ch3_b));
  Switch ch4 (.A(1'b1), .B(ch4_b));
  Switch ch1 (.A(1'b1), .B(ch1_b));
  Switch ch2 (.A(1'b1), .B(ch2_b));
  // Relay k3: pin names not known; wires that end beside it: ch3_b, 1'b1, ch4_b, 1'b0, k3_p5, 1'b0
  // Relay k4: pin names not known; wires that end beside it: 1'b1, ch1_b, k3_p5, 1'b0
  // Relay k1: pin names not known; wires that end beside it: 1'b1, ch2_b, k1_p3, 1'b0
  // Relay k2: pin names not known; wires that end beside it: 1'b1, k1_p3
  LED led_1 (.in(k1_p3));
  // RelayDT relaydt_1: pin names not known; wires that end beside it: k3_p5, 1'b1, 1'b0, relaydt_1_p4
  LED led_2 (.in(relaydt_1_p4));
endmodule
