// Logisim project 2 aula.circ as structural Verilog: 1 circuit, main circuit main
module main (
  input  in_1,
  input  \nand ,
  input  in_3,
  input  in_4,
  input  in_5,
  input  in_6,
  input  in_7,
  input  \nor ,
  input  in_9,
  input  in_10,
  input  in_11,
  input  in_12,
  input  in_13,
  input  in_14,
  input  in_15,
  input  in_16,
  input  in_17,
  input  in_18,
  input  in_19,
  input  in_20,
  input  in_21,
  input  in_22,
  input  in_23,
  input  in_24,
  output s,
  output out_26,
  output out_27,
  output out_28,
  output out_29,
  output out_30,
  output out_31,
  output out_32,
  output out_33,
  output out_34,
  output out_35,
  output out_36,
  output out_37,
  output out_38
);

  wire and_3_out, and_4_out, button_1_out, button_2_out, button_3_out, button_4_out, button_5_out,
       button_6_out, button_7_out, button_9_out, button_11_out, button_13_out, button_15_out, button_16_out,
       button_17_out, button_18_out, click_out, digital_oscilloscope_5_p1, digital_oscilloscope_6_p2,
       digital_oscilloscope_7_p1, digital_oscilloscope_8_p7, not_1_out, not_2_out, not_4_out, not_5_out,
       not_6_out, not_7_out, not_9_out, not_10_out, or_1_out, reset_out;

  and e (s, in_1, in_3, in_5);
  or ou (out_27, in_7, in_9, in_11);
  not n (out_29, in_13);
  // AND_Gate and_1 is placed but not wired
  and and_2 (out_31, in_17, in_21);
  not not_1 (not_1_out, in_17);
  not not_2 (not_2_out, in_21);
  or or_1 (or_1_out, not_1_out, not_2_out);
  not not_3 (out_35, or_1_out);
  Button click (.out(click_out));
  Button reset (.out(reset_out));
  Button button_1 (.out(button_1_out));
  Button button_2 (.out(button_2_out));
  Button button_3 (.out(button_3_out));
  Button button_4 (.out(button_4_out));
  Button button_5 (.out(button_5_out));
  Button button_6 (.out(button_6_out));
  // Digital_Oscilloscope digital_oscilloscope_1: pin names not known; wires that end beside it: click_out, in_1, in_3, in_5
  // Digital_Oscilloscope digital_oscilloscope_2: pin names not known; wires that end beside it: s, button_1_out, in_7, in_9, in_11, out_27, reset_out
  // Digital_Oscilloscope digital_oscilloscope_3: pin names not known; wires that end beside it: button_3_out, in_13, in_15, in_16, out_29, button_2_out
  // Digital_Oscilloscope digital_oscilloscope_4: pin names not known; wires that end beside it: button_5_out, in_17, in_21, out_31, out_35, button_4_out, button_6_out
  not not_4 (not_4_out, in_18);
  not not_5 (not_5_out, in_22);
  nand ne (out_26, \nand , in_4, in_6);
  nor nou (out_28, \nor , in_10, in_12);
  nand nand_1 (out_30, in_14, in_14, in_14);
  nand nand_2 (out_32, in_18, in_22);
  or or_2 (out_36, not_4_out, not_5_out);
  Button button_7 (.out(button_7_out));
  // Digital_Oscilloscope digital_oscilloscope_5: pin names not known; wires that end beside it: digital_oscilloscope_5_p1, \nand , in_4, in_6
  Button button_8 (.out(digital_oscilloscope_5_p1));
  Button button_9 (.out(button_9_out));
  // Digital_Oscilloscope digital_oscilloscope_6: pin names not known; wires that end beside it: out_26, digital_oscilloscope_6_p2, \nor , in_10, in_12, out_28, button_9_out
  Button button_10 (.out(digital_oscilloscope_6_p2));
  Button button_11 (.out(button_11_out));
  // Digital_Oscilloscope digital_oscilloscope_7: pin names not known; wires that end beside it: digital_oscilloscope_7_p1, in_14, in_14, in_14, out_30, button_11_out
  Button button_12 (.out(digital_oscilloscope_7_p1));
  Button button_13 (.out(button_13_out));
  // Digital_Oscilloscope digital_oscilloscope_8: pin names not known; wires that end beside it: button_7_out, in_18, in_22, out_32, out_36, button_13_out, digital_oscilloscope_8_p7
  Button button_14 (.out(digital_oscilloscope_8_p7));
  not not_6 (not_6_out, in_19);
  not not_7 (not_7_out, in_23);
  or or_3 (out_33, in_19, in_23);
  and and_3 (and_3_out, not_6_out, not_7_out);
  not not_8 (out_37, and_3_out);
  Button button_15 (.out(button_15_out));
  Button button_16 (.out(button_16_out));
  // Digital_Oscilloscope digital_oscilloscope_9: pin names not known; wires that end beside it: button_15_out, in_19, in_23, out_33, out_37, button_16_out
  // OR_Gate or_4 has open pins: out=out_34
  not not_9 (not_9_out, in_20);
  not not_10 (not_10_out, in_24);
  and and_4 (and_4_out, not_9_out, not_10_out);
  not not_11 (out_38, and_4_out);
  Button button_17 (.out(button_17_out));
  Button button_18 (.out(button_18_out));
  // Digital_Oscilloscope digital_oscilloscope_10: pin names not known; wires that end beside it: button_17_out, in_20, in_24, out_34, out_38, button_18_out

  // Notes on the sheet:
  //   and
  //   or
  //   not
  //   and
endmodule
