// Digital circuit 2 aula.dig as structural Verilog
module _2_aula (
);

  wire ch1_2_b, ch1_3_b, ch1_b, ch2_2_b, ch2_3_b, ch2_b, e1_2_b, e1_b, e2_b, e4_b, e5_b, k1_2_p3, k1_3_p5,
       k1_4_p3, k1_p3, k2_2_p4, k2_3_p3, k2_4_p2, k2_5_p5, k2_6_p3, k2_p2, k3_p5, k6_p5, relay_1_p2,
       relaydt_1_p2, relaydt_2_p2, switch_1_b;

  Switch e2 (.A(1'b1), .B(e2_b));
  Switch e5 (.A(1'b1), .B(e5_b));
  Switch e1 (.A(1'b1), .B(e1_b));
  Switch e1_2 (.A(1'b1), .B(e1_2_b));
  Switch ch1 (.A(1'b1), .B(ch1_b));
  Switch ch2 (.A(1'b1), .B(ch2_b));
  // Relay k3: pin names not known; wires that end beside it: e2_b, 1'b1, e5_b, 1'b0, k3_p5, 1'b0
  // Relay k4: pin names not known; wires that end beside it: 1'b1, e1_2_b, k3_p5, 1'b0
  // Relay k1: pin names not known; wires that end beside it: 1'b1, ch1_b, k1_p3, 1'b0
  // Relay k1_2: pin names not known; wires that end beside it: 1'b1, ch2_b, k1_2_p3, 1'b0
  // Relay k2: pin names not known; wires that end beside it: k1_2_p3, k2_p2, k2_p2, 1'b0
  LED \or  (.in(k3_p5));
  // Relay k2_2: pin names not known; wires that end beside it: e1_b, k1_p3, 1'b0, k2_2_p4
  // RelayDT relaydt_1: pin names not known; wires that end beside it: 1'b1, relaydt_1_p2
  LED \and  (.in(k2_2_p4));
  LED \nand  (.in(relaydt_1_p2));
  Switch e4 (.A(1'b1), .B(e4_b));
  Switch switch_1 (.A(1'b1), .B(switch_1_b));
  // Relay k6: pin names not known; wires that end beside it: e4_b, 1'b1, switch_1_b, 1'b0, k6_p5, 1'b0
  // Relay relay_1: pin names not known; wires that end beside it: k6_p5, relay_1_p2
  LED and_2 (.in(relay_1_p2));
  Switch ch1_2 (.A(1'b1), .B(ch1_2_b));
  Switch ch2_2 (.A(1'b1), .B(ch2_2_b));
  Switch ch1_3 (.A(1'b1), .B(ch1_3_b));
  Switch ch2_3 (.A(1'b1), .B(ch2_3_b));
  // Relay k1_3: pin names not known; wires that end beside it: ch1_2_b, 1'b1, ch2_2_b, 1'b0, k1_3_p5, 1'b0
  // Relay k2_3: pin names not known; wires that end beside it: 1'b1, ch1_3_b, k2_3_p3, 1'b0
  // Relay k1_4: pin names not known; wires that end beside it: 1'b1, ch2_3_b, k1_4_p3, 1'b0
  // Relay k2_4: pin names not known; wires that end beside it: 1'b1, k2_4_p2
  // RelayDT k2_5: pin names not known; wires that end beside it: ch2_2_b, k1_3_p5, ch1_2_b, 1'b0, k2_5_p5, 1'b0
  // RelayDT k1_5: pin names not known; wires that end beside it: k2_3_p3, ch2_3_b, k2_5_p5, 1'b0
  // RelayDT k2_6: pin names not known; wires that end beside it: k1_4_p3, ch1_3_b, k2_6_p3, 1'b0, k2_6_p3, 1'b0
  // RelayDT k1_6: pin names not known; wires that end beside it: k2_4_p2, k2_6_p3
  LED \xor  (.in(k2_5_p5));
  // RelayDT relaydt_2: pin names not known; wires that end beside it: 1'b1, relaydt_2_p2
  LED \xnor  (.in(relaydt_2_p2));
endmodule
