// Logisim project 3aula.circ as structural Verilog: 7 circuits, main circuit main
module main (
  input  in_1,
  input  in_2,
  input  te,
  input  b,
  input  a,
  output out_6,
  output out_7,
  output out_8,
  output out_9,
  output ts,
  output s
);

  xor xor_1 (out_6, in_1, in_2);
  and and_1 (out_7, in_1, in_2);
  meios meios_1 (.a(in_1), .b(in_2), .s(out_8), .st(out_9));
  fulls fulls_1 (.te(te), .a(b), .b(a), .ts(ts), .s(s));
endmodule

module calculadorahexa (
  input  a0,
  input  b0,
  input  a1,
  input  b1,
  input  a2,
  input  b2,
  input  b3,
  input  a3,
  input  in_9,
  input  in_10,
  input  in_11,
  input  in_12,
  input  in_13,
  input  in_14,
  input  in_15,
  input  in_16,
  output out_17,
  output out_18,
  output out_19,
  output out_20,
  output out_21,
  output out_22,
  output out_23,
  output out_24,
  output out_25,
  output out_26
);

  wire fulls_1_s, fulls_2_s, fullssub_1_ts, fullssub_2_ts, meios_1_st, meiosub_1_ts;

  meios meios_1 (.a(a0), .b(b0), .s(out_17), .st(meios_1_st));
  fulls fulls_1 (.te(meios_1_st), .a(a1), .b(b1), .ts(out_18), .s(fulls_1_s));
  fulls fulls_2 (.te(fulls_1_s), .a(a2), .b(b2), .ts(out_19), .s(fulls_2_s));
  fulls fulls_3 (.te(fulls_2_s), .a(b3), .b(a3), .ts(out_20), .s(out_21));
  meiosub meiosub_1 (.a(in_12), .b(in_16), .s(out_26), .ts(meiosub_1_ts));
  fullssub fullssub_1 (.te(meiosub_1_ts), .a(in_11), .b(in_15), .s(out_25), .ts(fullssub_1_ts));
  fullssub fullssub_2 (.te(fullssub_1_ts), .a(in_10), .b(in_14), .s(out_24), .ts(fullssub_2_ts));
  fullssub fullssub_3 (.te(fullssub_2_ts), .a(in_9), .b(in_13), .s(out_23), .ts(out_22));
  Hex_Digit_Display hex_digit_display_1 (.value({3'b000, out_21}));  // open: dp
  Hex_Digit_Display hex_digit_display_2 (.value({out_20, out_19, out_18, out_17}));  // open: dp
  Hex_Digit_Display hex_digit_display_3 (.value({a3, b2, b1, b0}));  // open: dp
  Hex_Digit_Display hex_digit_display_4 (.value({b3, a2, a1, a0}));  // open: dp
  Hex_Digit_Display hex_digit_display_5 (.value({in_9, in_10, in_11, in_12}));  // open: dp
  Hex_Digit_Display hex_digit_display_6 (.value({in_13, in_14, in_15, in_16}));  // open: dp
  Hex_Digit_Display hex_digit_display_7 (.value({3'b000, out_22}));  // open: dp
  Hex_Digit_Display hex_digit_display_8 (.value({out_23, out_24, out_25, out_26}));  // open: dp
endmodule

module subtrator (
  input  a0,
  input  b0,
  input  a1,
  input  b1,
  input  a2,
  input  b2,
  input  b3,
  input  a3,
  input  in_9,
  input  in_10,
  input  in_11,
  input  in_12,
  input  in_13,
  input  in_14,
  input  in_15,
  input  in_16,
  output out_17,
  output out_18,
  output out_19,
  output out_20,
  output out_21,
  output out_22,
  output out_23,
  output out_24,
  output out_25,
  output out_26
);

  wire fullssub_1_ts, fullssub_2_ts, fullssub_4_ts, fullssub_5_ts, meiosub_1_ts, meiosub_2_ts;

  meiosub meiosub_1 (.a(a0), .b(b0), .s(out_17), .ts(meiosub_1_ts));
  fullssub fullssub_1 (.te(meiosub_1_ts), .a(a1), .b(b1), .s(out_18), .ts(fullssub_1_ts));
  fullssub fullssub_2 (.te(fullssub_1_ts), .a(a2), .b(b2), .s(out_19), .ts(fullssub_2_ts));
  fullssub fullssub_3 (.te(fullssub_2_ts), .a(b3), .b(a3), .s(out_20), .ts(out_21));
  meiosub meiosub_2 (.a(in_12), .b(in_16), .s(out_26), .ts(meiosub_2_ts));
  fullssub fullssub_4 (.te(meiosub_2_ts), .a(in_11), .b(in_15), .s(out_25), .ts(fullssub_4_ts));
  fullssub fullssub_5 (.te(fullssub_4_ts), .a(in_10), .b(in_14), .s(out_24), .ts(fullssub_5_ts));
  fullssub fullssub_6 (.te(fullssub_5_ts), .a(in_9), .b(in_13), .s(out_23), .ts(out_22));
  Hex_Digit_Display hex_digit_display_1 (.value({3'b000, out_21}));  // open: dp
  Hex_Digit_Display hex_digit_display_2 (.value({out_20, out_19, out_18, out_17}));  // open: dp
  Hex_Digit_Display hex_digit_display_3 (.value({a3, b2, b1, b0}));  // open: dp
  Hex_Digit_Display hex_digit_display_4 (.value({b3, a2, a1, a0}));  // open: dp
  Hex_Digit_Display hex_digit_display_5 (.value({in_9, in_10, in_11, in_12}));  // open: dp
  Hex_Digit_Display hex_digit_display_6 (.value({in_13, in_14, in_15, in_16}));  // open: dp
  Hex_Digit_Display hex_digit_display_7 (.value({3'b000, out_22}));  // open: dp
  Hex_Digit_Display hex_digit_display_8 (.value({out_23, out_24, out_25, out_26}));  // open: dp
endmodule

module meios (
  input  a,
  input  b,
  output s,
  output st
);

  wire and_1_out, and_2_out, not_1_out, not_2_out;

  not not_1 (not_1_out, a);
  not not_2 (not_2_out, b);
  and and_1 (and_1_out, not_2_out, a);
  and and_2 (and_2_out, b, not_1_out);
  and and_3 (st, b, a);
  or or_1 (s, and_1_out, and_2_out);
endmodule

module fulls (
  input  te,
  input  a,
  input  b,
  output ts,
  output s
);

  wire and_1_out, and_2_out, and_3_out, and_4_out, and_5_out, and_6_out, and_7_out, not_1_out, not_2_out,
       not_3_out;

  not not_1 (not_1_out, te);
  not not_2 (not_2_out, a);
  not not_3 (not_3_out, b);
  and and_1 (and_1_out, not_1_out, not_3_out, a);
  and and_2 (and_2_out, not_1_out, b, not_2_out);
  and and_3 (and_3_out, te, not_3_out, not_2_out);
  and and_4 (and_4_out, te, b, a);
  and and_5 (and_5_out, b, a);
  and and_6 (and_6_out, te, a);
  and and_7 (and_7_out, te, b);
  or or_1 (ts, and_1_out, and_2_out, and_3_out, and_4_out);
  or or_2 (s, and_5_out, and_6_out, and_7_out);
endmodule

module meiosub (
  input  a,
  input  b,
  output s,
  output ts
);

  wire and_1_out, and_2_out, not_1_out, not_2_out;

  not not_1 (not_1_out, a);
  not not_2 (not_2_out, b);
  and and_1 (and_1_out, not_2_out, a);
  and and_2 (and_2_out, b, not_1_out);
  and and_3 (ts, not_1_out, b);
  or or_1 (s, and_1_out, and_2_out);
endmodule

module fullssub (
  input  te,
  input  a,
  input  b,
  output s,
  output ts
);

  wire and_1_out, and_2_out, and_3_out, and_4_out, not_1_out, not_2_out, not_3_out;

  not not_1 (not_1_out, te);
  not not_2 (not_2_out, a);
  not not_3 (not_3_out, b);
  and and_1 (and_1_out, not_1_out, not_2_out, b);
  and and_2 (and_2_out, not_1_out, a, not_3_out);
  and and_3 (and_3_out, te, not_2_out, not_3_out);
  and and_4 (and_4_out, te, a, b);
  and and_5 (ts, not_1_out, not_2_out, b);
  or or_1 (s, and_1_out, and_2_out, and_3_out, and_4_out);
endmodule
