// Logisim project 4aula.circ as structural Verilog: 2 circuits, main circuit main
module main (
  input  in_1,
  input  in_2,
  input  in_3,
  output out_4,
  output out_5,
  output out_6,
  output out_7
);

  wire and_1_out, and_2_out, and_3_out, xor_1_out;

  xor xor_1 (xor_1_out, in_1, in_2);
  and and_1 (and_1_out, in_1, in_2);
  and and_2 (and_2_out, in_1, in_3);
  and and_3 (and_3_out, in_2, in_3);
  xor xor_2 (out_5, xor_1_out, in_3);
  or or_1 (out_7, and_1_out, and_2_out, and_3_out);
  help help_1 (.te(in_1), .b(in_2), .a(in_3), .s(out_4), .ts(out_6));
endmodule

module help (
  input  te,
  input  b,
  input  a,
  output s,
  output ts
);

  wire and_1_out, and_2_out, and_3_out, and_4_out, and_5_out, and_6_out, and_7_out, not_1_out, not_2_out,
       not_3_out;

  not not_1 (not_1_out, te);
  not not_2 (not_2_out, b);
  not not_3 (not_3_out, a);
  and and_1 (and_1_out, not_3_out, not_2_out, te);
  and and_2 (and_2_out, not_3_out, b, not_1_out);
  and and_3 (and_3_out, a, not_2_out, not_1_out);
  and and_4 (and_4_out, a, b, te);
  and and_5 (and_5_out, b, te);
  and and_6 (and_6_out, a, te);
  and and_7 (and_7_out, a, b);
  or or_1 (s, and_1_out, and_2_out, and_3_out, and_4_out);
  or or_2 (ts, and_5_out, and_6_out, and_7_out);
endmodule
