// Logisim project 5aula.circ as structural Verilog: 3 circuits, main circuit main
module main (
  input  [7:0] in_1,
  input  [7:0] in_2,
  input  in_3,
  input  in_4,
  input  in_5,
  output [7:0] out_6
);

  wire botao1_out, botao2_out, clock_1_out;
  wire [7:0] alu_1_saida;

  Hex_Digit_Display hex_digit_display_1 (.value(out_6[7:4]));  // open: dp
  Hex_Digit_Display hex_digit_display_2 (.value(out_6[3:0]));  // open: dp
  Hex_Digit_Display hex_digit_display_3 (.value(in_2[7:4]));  // open: dp
  Hex_Digit_Display hex_digit_display_4 (.value(in_2[3:0]));  // open: dp
  Register register_1 (.D(alu_1_saida), .en(1'b1), .clk(clock_1_out), .Q(out_6), .clr(botao2_out));
  alu alu_1 (.e1b(out_6), .e2b(in_2), .e1(in_3), .e2(in_4), .e3(in_5), .saida(alu_1_saida));
  Clock clock_1 (.out(clock_1_out));
  Button botao1 (.out(botao1_out));
  Button botao2 (.out(botao2_out));
  Hex_Digit_Display hex_digit_display_5 (.value(out_6[7:4]));  // open: dp
  Hex_Digit_Display hex_digit_display_6 (.value(out_6[3:0]));  // open: dp
endmodule

module alu (
  input  [7:0] e1b,
  input  [7:0] e2b,
  input  e1,
  input  e2,
  input  e3,
  output [7:0] saida
);

  wire decodificador3x4_1_s1, decodificador3x4_1_s2, decodificador3x4_1_s3, decodificador3x4_1_s4;
  wire [7:0] adder_1_out, divider_1_out, multiplier_1_out, subtractor_1_out;

  Adder adder_1 (.a(e1b), .b(e2b), .out(adder_1_out));  // open: cin, cout
  Subtractor subtractor_1 (.a(e1b), .b(e2b), .out(subtractor_1_out));  // open: bin, bout
  Multiplier multiplier_1 (.a(e1b), .b(e2b), .out(multiplier_1_out));  // open: cin, cout
  Divider divider_1 (.a(e1b), .b(e2b), .out(divider_1_out));  // open: upper, rem
  decodificador3x4 decodificador3x4_1 (
    .e1(e1), .e2(e2), .cs(e3), .s1(decodificador3x4_1_s1), .s2(decodificador3x4_1_s2),
    .s3(decodificador3x4_1_s3), .s4(decodificador3x4_1_s4));
  assign saida = decodificador3x4_1_s1 ? adder_1_out : 8'bz;  // Controlled_Buffer controlled_buffer_1
  assign saida = decodificador3x4_1_s2 ? subtractor_1_out : 8'bz;  // Controlled_Buffer controlled_buffer_2
  assign saida = decodificador3x4_1_s3 ? multiplier_1_out : 8'bz;  // Controlled_Buffer controlled_buffer_3
  assign saida = decodificador3x4_1_s4 ? divider_1_out : 8'bz;  // Controlled_Buffer controlled_buffer_4
endmodule

module decodificador3x4 (
  input  e1,
  input  e2,
  input  cs,
  output s1,
  output s2,
  output s3,
  output s4
);

  wire not_1_out, not_2_out;

  not not_1 (not_1_out, e1);
  not not_2 (not_2_out, e2);
  and and_1 (s1, cs, not_1_out, not_2_out);
  and and_2 (s2, cs, not_2_out, e1);
  and and_3 (s3, cs, e2, not_1_out);
  and and_4 (s4, cs, e1, e2);
endmodule
