// Logisim project 6 decodificador.circ as structural Verilog: 7 circuits, main circuit main
module main (
  input  [7:0] in_1,
  input  [7:0] in_2,
  input  in_3,
  input  in_4,
  input  in_5,
  input  in_6,
  output [7:0] out_7,
  output [2:0] out_8
);

  Hex_Digit_Display hex_digit_display_1 (.value(in_1[7:4]));  // open: dp
  Hex_Digit_Display hex_digit_display_2 (.value(in_1[3:0]));  // open: dp
  Hex_Digit_Display hex_digit_display_3 (.value(in_2[7:4]));  // open: dp
  Hex_Digit_Display hex_digit_display_4 (.value(in_2[3:0]));  // open: dp
  alu alu_1 (
    .ealu1(in_1), .elau2(in_2), .dec1(in_3), .dec2(in_4), .dec3(in_5), .dec4(in_6), .sdois({out_8, out_7}));  // open: sequacao, out_9
  Hex_Digit_Display hex_digit_display_5 (.value(out_7[7:4]));  // open: dp
  Hex_Digit_Display hex_digit_display_6 (.value(out_7[3:0]));  // open: dp
  LED led_1 (.in(out_8[2]));
  LED led_2 (.in(out_8[0]));
  LED led_3 (.in(out_8[1]));
endmodule

module alu (
  input  [7:0] ealu1,
  input  [7:0] elau2,
  input  dec1,
  input  dec2,
  input  dec3,
  input  dec4,
  output [7:0] sequacao,
  output [10:0] sdois,
  output [2:0] out_9
);

  wire dec4x8_1_div, dec4x8_1_mult, dec4x8_1_ouexclusivo, dec4x8_1_s6, dec4x8_1_soma, dec4x8_1_sub;
  wire [2:0] comparator_1_gt;
  wire [7:0] adder_1_out, divider_1_out, multiplier_1_out, ouexclusivo_1_sxor, subtractor_1_out;

  Hex_Digit_Display hex_digit_display_1 (.value(ealu1[3:0]));  // open: dp
  Hex_Digit_Display hex_digit_display_2 (.value(ealu1[7:4]));  // open: dp
  Hex_Digit_Display hex_digit_display_3 (.value(elau2[3:0]));  // open: dp
  Hex_Digit_Display hex_digit_display_4 (.value(elau2[7:4]));  // open: dp
  Adder adder_1 (.a(ealu1), .b(elau2), .out(adder_1_out));  // open: cin, cout
  Subtractor subtractor_1 (.a(ealu1), .b(elau2), .out(subtractor_1_out));  // open: bin, bout
  Multiplier multiplier_1 (.a(ealu1), .b(elau2), .out(multiplier_1_out));  // open: cin, cout
  Divider divider_1 (.a(ealu1), .b(elau2), .out(divider_1_out));  // open: upper, rem
  ouexclusivo ouexclusivo_1 (.exor1(ealu1), .exor2(elau2), .sxor(ouexclusivo_1_sxor));
  Comparator comparator_1 (
    .a(ealu1), .b(elau2), .gt(comparator_1_gt[0]), .eq(comparator_1_gt[1]), .lt(comparator_1_gt[2]));
  dec4x8 dec4x8_1 (
    .e1(dec1), .e2(dec2), .e3(dec3), .cs(dec4), .soma(dec4x8_1_soma), .sub(dec4x8_1_sub),
    .mult(dec4x8_1_mult), .div(dec4x8_1_div), .ouexclusivo(dec4x8_1_ouexclusivo), .s6(dec4x8_1_s6));  // open: s7, s8
  assign sdois[7:0] = dec4x8_1_soma ? adder_1_out : 8'bz;  // Controlled_Buffer controlled_buffer_1
  assign sdois[7:0] = dec4x8_1_sub ? subtractor_1_out : 8'bz;  // Controlled_Buffer controlled_buffer_2
  assign sdois[7:0] = dec4x8_1_mult ? multiplier_1_out : 8'bz;  // Controlled_Buffer controlled_buffer_3
  assign sdois[7:0] = dec4x8_1_div ? divider_1_out : 8'bz;  // Controlled_Buffer controlled_buffer_4
  assign sdois[7:0] = dec4x8_1_ouexclusivo ? ouexclusivo_1_sxor : 8'bz;  // Controlled_Buffer controlled_buffer_5
  assign out_9 = dec4x8_1_s6 ? comparator_1_gt : 3'bz;  // Controlled_Buffer controlled_buffer_6
  Hex_Digit_Display hex_digit_display_5 (.value(sdois[7:4]));  // open: dp
  Hex_Digit_Display hex_digit_display_6 (.value(sdois[3:0]));  // open: dp

  assign sdois[10:8] = out_9;
  assign sequacao = sdois[7:0];
endmodule

module ouexclusivo (
  input  [7:0] exor1,
  input  [7:0] exor2,
  output [7:0] sxor
);

  xor xor_1 (sxor[0], exor1[0], exor2[0]);
  xor xor_2 (sxor[1], exor1[1], exor2[1]);
  xor xor_3 (sxor[2], exor1[2], exor2[2]);
  xor xor_4 (sxor[3], exor1[3], exor2[3]);
  xor xor_5 (sxor[4], exor1[4], exor2[4]);
  xor xor_6 (sxor[5], exor1[5], exor2[5]);
  xor xor_7 (sxor[6], exor1[6], exor2[6]);
  xor xor_8 (sxor[7], exor1[7], exor2[7]);
endmodule

module dec4x8 (
  input  e1,
  input  e2,
  input  e3,
  input  cs,
  output soma,
  output sub,
  output mult,
  output div,
  output ouexclusivo,
  output s6,
  output s7,
  output s8
);

  wire not_1_out, not_2_out, not_3_out;

  not not_1 (not_1_out, e1);
  not not_2 (not_2_out, e2);
  not not_3 (not_3_out, e3);
  and and_1 (soma, not_1_out, not_2_out, not_3_out, cs);
  and and_2 (sub, e1, not_2_out, not_3_out, cs);
  and and_3 (mult, not_1_out, e2, not_3_out, cs);
  and and_4 (div, not_1_out, not_2_out, e3, cs);
  and and_5 (ouexclusivo, e1, e2, e3, cs);
  and and_6 (s6, e1, e2, not_3_out, cs);

  assign s7 = 1'b0;
  assign s8 = 1'b0;
endmodule

module comparador (
  input  ecomp1,
  input  ecomp2,
  output maior,
  output igual,
  output menor
);

  wire meiocomp_1_aigualb, meiocomp_1_amaiorb, meiocomp_1_amenorb;

  meiocomp meiocomp_1 (
    .a(ecomp1), .b(ecomp2), .amenorb(meiocomp_1_amenorb), .AigualB(meiocomp_1_aigualb),
    .AmaiorB(meiocomp_1_amaiorb));
  fullcomp fullcomp_1 (
    .a(ecomp1), .b(ecomp2), .AmenorB(meiocomp_1_amenorb), .AigualB(meiocomp_1_aigualb),
    .AmaiorB(meiocomp_1_amaiorb), .sAmenorB(maior), .sAigualB(igual), .sAmaiorB(menor));
endmodule

module meiocomp (
  input  a,
  input  b,
  output amenorb,
  output AigualB,
  output AmaiorB
);

  wire and_2_out, and_3_out, not_1_out, not_2_out;

  not not_1 (not_1_out, a);
  not not_2 (not_2_out, b);
  and and_1 (amenorb, not_1_out, b);
  and and_2 (and_2_out, not_1_out, not_2_out);
  and and_3 (and_3_out, a, b);
  and and_4 (AmaiorB, a, not_2_out);
  or or_1 (AigualB, and_2_out, and_3_out);
endmodule

module fullcomp (
  input  a,
  input  b,
  input  AmenorB,
  input  AigualB,
  input  AmaiorB,
  output sAmenorB,
  output sAigualB,
  output sAmaiorB
);

  wire and_1_out, and_2_out, and_3_out, and_4_out, and_5_out, and_6_out, and_7_out, and_8_out, and_9_out,
       and_10_out, not_1_out, not_2_out, not_3_out, not_4_out, not_5_out;

  not not_1 (not_1_out, a);
  not not_2 (not_2_out, b);
  not not_3 (not_3_out, AmenorB);
  not not_4 (not_4_out, AigualB);
  not not_5 (not_5_out, AmaiorB);
  and and_1 (and_1_out, not_2_out, AmenorB, not_4_out, not_5_out);
  and and_2 (and_2_out, a, not_2_out, not_3_out, not_4_out, AmaiorB);
  and and_3 (and_3_out, a, not_2_out, not_3_out, AigualB, not_5_out);
  and and_4 (and_4_out, a, AmenorB, not_4_out, not_5_out);
  and and_5 (and_5_out, not_1_out, not_2_out, not_3_out, AigualB, not_5_out);
  or or_1 (sAigualB, and_5_out, and_6_out);
  and and_6 (and_6_out, a, b, not_3_out, not_5_out);
  and and_7 (and_7_out, not_1_out, not_3_out, not_4_out, AmaiorB);
  and and_8 (and_8_out, b, not_3_out, not_4_out, AmaiorB);
  and and_9 (and_9_out, not_1_out, b, not_3_out, AigualB, not_5_out);
  and and_10 (and_10_out, not_1_out, b, AmenorB, not_4_out, not_5_out);
  or or_2 (sAmenorB, and_1_out, and_2_out, and_3_out, and_4_out);
  or or_3 (sAmaiorB, and_7_out, and_8_out, and_9_out, and_10_out);
endmodule
