// Logisim project 7multiplexador.circ as structural Verilog: 10 circuits, main circuit main
module main (
  input  in_1,
  input  in_2,
  input  in_3,
  input  in_4
);

  wire button_1_out, clock_1_out, dm1x4_1_s0m, dm1x4_1_s1m, dm1x4_1_s2m, dm1x4_1_s3m, m4x1_1_s0m;
  wire [1:0] c2b_1_out_3;

  Clock clock_1 (.out(clock_1_out));
  Button button_1 (.out(button_1_out));
  c2b c2b_1 (.in_1(clock_1_out), .in_2(button_1_out), .out_3(c2b_1_out_3));
  m4x1 m4x1_1 (
    .e1md(c2b_1_out_3[0]), .e2md(c2b_1_out_3[1]), .e1m(in_1), .e2m(in_2), .e3m(in_3), .e4m(in_4),
    .s0m(m4x1_1_s0m));
  dm1x4 dm1x4_1 (
    .e2md(c2b_1_out_3[1]), .e1md(c2b_1_out_3[0]), .in_3(m4x1_1_s0m), .s0m(dm1x4_1_s0m), .s1m(dm1x4_1_s1m),
    .s2m(dm1x4_1_s2m), .s3m(dm1x4_1_s3m));
  LED led_1 (.in(dm1x4_1_s0m));
  LED led_2 (.in(dm1x4_1_s1m));
  LED led_3 (.in(dm1x4_1_s2m));
  LED led_4 (.in(dm1x4_1_s3m));
endmodule

module dec2x4 (
  input  e2,
  input  e1,
  output s0,
  output s1,
  output s2,
  output s3
);

  wire not_1_out, not_2_out;

  not not_1 (not_1_out, e2);
  not not_2 (not_2_out, e1);
  and and_1 (s0, not_1_out, not_2_out);
  and and_2 (s1, not_1_out, e1);
  and and_3 (s2, e2, not_2_out);
  and and_4 (s3, e2, e1);
endmodule

module m4x1 (
  input  e1md,
  input  e2md,
  input  e1m,
  input  e2m,
  input  e3m,
  input  e4m,
  output s0m
);

  wire and_1_out, and_2_out, and_3_out, and_4_out, dec2x4_1_s0, dec2x4_1_s1, dec2x4_1_s2, dec2x4_1_s3;

  dec2x4 dec2x4_1 (.e2(e1md), .e1(e2md), .s0(dec2x4_1_s0), .s1(dec2x4_1_s1), .s2(dec2x4_1_s2), .s3(dec2x4_1_s3));
  and and_1 (and_1_out, e1m, dec2x4_1_s0);
  and and_2 (and_2_out, e2m, dec2x4_1_s1);
  and and_3 (and_3_out, e3m, dec2x4_1_s2);
  and and_4 (and_4_out, e4m, dec2x4_1_s3);
  or or_1 (s0m, and_1_out, and_2_out, and_3_out, and_4_out);
endmodule

module dm1x4 (
  input  e2md,
  input  e1md,
  input  in_3,
  output s0m,
  output s1m,
  output s2m,
  output s3m
);

  wire dec2x4_1_s0, dec2x4_1_s1, dec2x4_1_s2, dec2x4_1_s3;

  dec2x4 dec2x4_1 (.e2(e2md), .e1(e1md), .s0(dec2x4_1_s0), .s1(dec2x4_1_s1), .s2(dec2x4_1_s2), .s3(dec2x4_1_s3));
  and and_1 (s0m, in_3, dec2x4_1_s0);
  and and_2 (s1m, in_3, dec2x4_1_s1);
  and and_3 (s2m, in_3, dec2x4_1_s2);
  and and_4 (s3m, in_3, dec2x4_1_s3);
endmodule

module c2b (
  input  in_1,
  input  in_2,
  output [1:0] out_3
);

  wire [1:0] adder_1_out;

  Register #(.width(2)) register_1 (.D(adder_1_out), .en(1'b1), .clk(in_1), .Q(out_3), .clr(in_2));
  Adder #(.width(2)) adder_1 (.a(out_3), .b(2'b01), .out(adder_1_out));  // open: cin, cout
endmodule

module aula2main (
  input  in_1,
  input  in_2,
  input  in_3,
  input  in_4,
  input  in_5,
  input  in_6,
  input  in_7,
  input  in_8
);

  wire aula2dm1x8_1_out_5, aula2dm1x8_1_out_6, aula2dm1x8_1_out_7, aula2dm1x8_1_out_8, aula2dm1x8_1_out_9,
       aula2dm1x8_1_out_10, aula2dm1x8_1_out_11, aula2dm1x8_1_out_12, aula2mult8x1_1_out_12, button_1_out,
       clock_1_out;
  wire [2:0] aula2c3b_1_out_3;

  Clock clock_1 (.out(clock_1_out));
  Button button_1 (.out(button_1_out));
  aula2c3b aula2c3b_1 (.in_1(clock_1_out), .in_2(button_1_out), .out_3(aula2c3b_1_out_3));
  aula2mult8x1 aula2mult8x1_1 (
    .edec1(aula2c3b_1_out_3[2]), .edec2(aula2c3b_1_out_3[1]), .edec0(aula2c3b_1_out_3[0]), .in_4(in_1),
    .in_5(in_2), .in_6(in_3), .in_7(in_4), .in_8(in_5), .in_9(in_6), .in_10(in_7), .in_11(in_8),
    .out_12(aula2mult8x1_1_out_12));
  aula2dm1x8 aula2dm1x8_1 (
    .in_1(aula2c3b_1_out_3[2]), .in_2(aula2c3b_1_out_3[1]), .in_3(aula2c3b_1_out_3[0]),
    .edm(aula2mult8x1_1_out_12), .out_5(aula2dm1x8_1_out_5), .out_6(aula2dm1x8_1_out_6),
    .out_7(aula2dm1x8_1_out_7), .out_8(aula2dm1x8_1_out_8), .out_9(aula2dm1x8_1_out_9),
    .out_10(aula2dm1x8_1_out_10), .out_11(aula2dm1x8_1_out_11), .out_12(aula2dm1x8_1_out_12));
  LED led_1 (.in(aula2dm1x8_1_out_5));
  LED led_2 (.in(aula2dm1x8_1_out_6));
  LED led_3 (.in(aula2dm1x8_1_out_7));
  LED led_4 (.in(aula2dm1x8_1_out_8));
  LED led_5 (.in(aula2dm1x8_1_out_9));
  LED led_6 (.in(aula2dm1x8_1_out_10));
  LED led_7 (.in(aula2dm1x8_1_out_11));
  LED led_8 (.in(aula2dm1x8_1_out_12));
endmodule

module aula2dec3x8 (
  input  e1,
  input  e2,
  input  e0,
  output s0,
  output s1,
  output s2,
  output s3,
  output s4,
  output s5,
  output s6,
  output s7
);

  wire not_1_out, not_2_out, not_3_out;

  not not_1 (not_1_out, e1);
  not not_2 (not_2_out, e2);
  not not_3 (not_3_out, e0);
  and and_1 (s0, not_1_out, not_2_out, not_3_out);
  and and_2 (s1, not_1_out, not_2_out, e0);
  and and_3 (s2, not_1_out, e2, not_3_out);
  and and_4 (s3, not_1_out, e2, e0);
  and and_5 (s4, e1, not_2_out, not_3_out);
  and and_6 (s5, e1, not_2_out, e0);
  and and_7 (s6, e1, e2, not_3_out);
  and and_8 (s7, e1, e2, e0);
endmodule

module aula2mult8x1 (
  input  edec1,
  input  edec2,
  input  edec0,
  input  in_4,
  input  in_5,
  input  in_6,
  input  in_7,
  input  in_8,
  input  in_9,
  input  in_10,
  input  in_11,
  output out_12
);

  wire and_1_out, and_2_out, and_3_out, and_4_out, and_5_out, and_6_out, and_7_out, and_8_out,
       aula2dec3x8_1_s0, aula2dec3x8_1_s1, aula2dec3x8_1_s2, aula2dec3x8_1_s3, aula2dec3x8_1_s4,
       aula2dec3x8_1_s5, aula2dec3x8_1_s6, aula2dec3x8_1_s7;

  aula2dec3x8 aula2dec3x8_1 (
    .e1(edec1), .e2(edec2), .e0(edec0), .s0(aula2dec3x8_1_s0), .s1(aula2dec3x8_1_s1), .s2(aula2dec3x8_1_s2),
    .s3(aula2dec3x8_1_s3), .s4(aula2dec3x8_1_s4), .s5(aula2dec3x8_1_s5), .s6(aula2dec3x8_1_s6),
    .s7(aula2dec3x8_1_s7));
  and and_1 (and_1_out, in_4, aula2dec3x8_1_s0);
  and and_2 (and_2_out, in_5, aula2dec3x8_1_s1);
  and and_3 (and_3_out, in_6, aula2dec3x8_1_s2);
  and and_4 (and_4_out, in_7, aula2dec3x8_1_s3);
  and and_5 (and_5_out, in_8, aula2dec3x8_1_s4);
  and and_6 (and_6_out, in_9, aula2dec3x8_1_s5);
  and and_7 (and_7_out, in_10, aula2dec3x8_1_s6);
  and and_8 (and_8_out, in_11, aula2dec3x8_1_s7);
  or or_1 (out_12, and_1_out, and_2_out, and_3_out, and_4_out, and_5_out, and_6_out, and_7_out, and_8_out);
endmodule

module aula2c3b (
  input  in_1,
  input  in_2,
  output [2:0] out_3
);

  wire [2:0] adder_1_out;

  Adder #(.width(3)) adder_1 (.a(out_3), .b(3'b001), .out(adder_1_out));  // open: cin, cout
  Register #(.width(3)) register_1 (.D(adder_1_out), .en(1'b1), .clk(in_1), .Q(out_3), .clr(in_2));
endmodule

module aula2dm1x8 (
  input  in_1,
  input  in_2,
  input  in_3,
  input  edm,
  output out_5,
  output out_6,
  output out_7,
  output out_8,
  output out_9,
  output out_10,
  output out_11,
  output out_12
);

  wire aula2dec3x8_1_s0, aula2dec3x8_1_s1, aula2dec3x8_1_s2, aula2dec3x8_1_s3, aula2dec3x8_1_s4,
       aula2dec3x8_1_s5, aula2dec3x8_1_s6, aula2dec3x8_1_s7;

  aula2dec3x8 aula2dec3x8_1 (
    .e1(in_1), .e2(in_2), .e0(in_3), .s0(aula2dec3x8_1_s0), .s1(aula2dec3x8_1_s1), .s2(aula2dec3x8_1_s2),
    .s3(aula2dec3x8_1_s3), .s4(aula2dec3x8_1_s4), .s5(aula2dec3x8_1_s5), .s6(aula2dec3x8_1_s6),
    .s7(aula2dec3x8_1_s7));
  and and_1 (out_5, aula2dec3x8_1_s0, edm);
  and and_2 (out_6, aula2dec3x8_1_s1, edm);
  and and_3 (out_7, aula2dec3x8_1_s2, edm);
  and and_4 (out_8, aula2dec3x8_1_s3, edm);
  and and_5 (out_9, aula2dec3x8_1_s4, edm);
  and and_6 (out_10, aula2dec3x8_1_s5, edm);
  and and_7 (out_11, aula2dec3x8_1_s6, edm);
  and and_8 (out_12, aula2dec3x8_1_s7, edm);
endmodule
