// Logisim project aulas.circ as structural Verilog
module somador (
  input  in_1,
  input  in_2,
  input  in_3,
  input  in_4,
  input  in_5,
  input  in_6,
  input  in_7,
  input  in_8,
  output out_9,
  output out_10,
  output out_11,
  output out_12,
  output out_13
);

  wire fulls_1_ts, fulls_2_ts, meios_1_st;

  meios meios_1 (.a(in_4), .b(in_8), .s(out_13), .st(meios_1_st));
  fulls fulls_1 (.te(meios_1_st), .a(in_3), .b(in_7), .s(out_12), .ts(fulls_1_ts));
  fulls fulls_2 (.te(fulls_1_ts), .a(in_2), .b(in_6), .s(out_11), .ts(fulls_2_ts));
  fulls fulls_3 (.te(fulls_2_ts), .a(in_1), .b(in_5), .s(out_10), .ts(out_9));
  Hex_Digit_Display hex_digit_display_1 (.value({in_1, in_2, in_3, in_4}));  // open: dp
  Hex_Digit_Display hex_digit_display_2 (.value({3'b000, out_9}));  // open: dp
  Hex_Digit_Display hex_digit_display_3 (.value({in_5, in_6, in_7, in_8}));  // open: dp
  Hex_Digit_Display hex_digit_display_4 (.value({out_10, out_11, out_12, out_13}));  // open: dp
endmodule

module subtrator (
  input  in_1,
  input  in_2,
  input  in_3,
  input  in_4,
  input  in_5,
  input  in_6,
  input  in_7,
  input  in_8,
  output out_9,
  output out_10,
  output out_11,
  output out_12,
  output out_13
);

  wire fullssub_1_ts, fullssub_2_ts, meiosub_1_ts;

  meiosub meiosub_1 (.a(in_4), .b(in_8), .s(out_13), .ts(meiosub_1_ts));
  fullssub fullssub_1 (.te(meiosub_1_ts), .a(in_3), .b(in_7), .s(out_12), .ts(fullssub_1_ts));
  fullssub fullssub_2 (.te(fullssub_1_ts), .a(in_2), .b(in_6), .s(out_11), .ts(fullssub_2_ts));
  fullssub fullssub_3 (.te(fullssub_2_ts), .a(in_1), .b(in_5), .s(out_10), .ts(out_9));
  Hex_Digit_Display hex_digit_display_1 (.value({in_1, in_2, in_3, in_4}));  // open: dp
  Hex_Digit_Display hex_digit_display_2 (.value({3'b000, out_9}));  // open: dp
  Hex_Digit_Display hex_digit_display_3 (.value({in_5, in_6, in_7, in_8}));  // open: dp
  Hex_Digit_Display hex_digit_display_4 (.value({out_10, out_11, out_12, out_13}));  // open: dp
endmodule

module meios (
  input  a,
  input  b,
  output s,
  output st
);

  wire and_1_out, and_2_out, not_1_out, not_2_out;

  not not_1 (not_1_out, a);
  not not_2 (not_2_out, b);
  and and_1 (and_1_out, not_2_out, a);
  and and_2 (and_2_out, b, not_1_out);
  and and_3 (st, b, a);
  or or_1 (s, and_1_out, and_2_out);
endmodule

module fulls (
  input  te,
  input  a,
  input  b,
  output s,
  output ts
);

  wire and_1_out, and_2_out, and_3_out, and_4_out, and_5_out, and_6_out, and_7_out, not_1_out, not_2_out,
       not_3_out;

  not not_1 (not_1_out, te);
  not not_2 (not_2_out, a);
  not not_3 (not_3_out, b);
  and and_1 (and_1_out, not_1_out, not_2_out, b);
  and and_2 (and_2_out, not_1_out, a, not_3_out);
  and and_3 (and_3_out, te, not_2_out, not_3_out);
  and and_4 (and_4_out, te, a, b);
  and and_5 (and_5_out, a, b);
  and and_6 (and_6_out, te, b);
  and and_7 (and_7_out, te, a);
  or or_1 (s, and_1_out, and_2_out, and_3_out, and_4_out);
  or or_2 (ts, and_5_out, and_6_out, and_7_out);
endmodule

module meiosub (
  input  a,
  input  b,
  output s,
  output ts
);

  wire and_1_out, and_2_out, not_1_out, not_2_out;

  not not_1 (not_1_out, a);
  not not_2 (not_2_out, b);
  and and_1 (and_1_out, not_1_out, b);
  and and_2 (and_2_out, a, not_2_out);
  and and_3 (ts, not_1_out, b);
  or or_1 (s, and_1_out, and_2_out);
endmodule

module fullssub (
  input  te,
  input  a,
  input  b,
  output s,
  output ts
);

  wire and_1_out, and_2_out, and_3_out, and_4_out, and_5_out, and_6_out, and_7_out, not_1_out, not_2_out,
       not_3_out;

  not not_1 (not_1_out, te);
  not not_2 (not_2_out, a);
  not not_3 (not_3_out, b);
  and and_1 (and_1_out, not_1_out, not_2_out, b);
  and and_2 (and_2_out, not_1_out, a, not_3_out);
  and and_3 (and_3_out, te, not_2_out, not_3_out);
  and and_4 (and_4_out, te, a, b);
  and and_5 (and_5_out, not_2_out, b);
  and and_6 (and_6_out, te, not_2_out);
  and and_7 (and_7_out, te, b);
  or or_1 (s, and_1_out, and_2_out, and_3_out, and_4_out);
  or or_2 (ts, and_5_out, and_6_out, and_7_out);
endmodule

module comparador (
  input  A3,
  input  A2,
  input  A1,
  input  A0,
  input  B3,
  input  B2,
  input  B1,
  input  B0,
  output out_9,
  output out_10,
  output out_11
);

  wire fullcomp_1_aigualqb, fullcomp_1_amaiorqb, fullcomp_1_amenorqb, fullcomp_2_aigualqb,
       fullcomp_2_amaiorqb, fullcomp_2_amenorqb, meiocomp_1_aigualqb, meiocomp_1_amaiorqb,
       meiocomp_1_amenorqb;

  Hex_Digit_Display hex_digit_display_1 (.value({A3, A2, A1, A0}));  // open: dp
  Hex_Digit_Display hex_digit_display_2 (.value({B3, B2, B1, B0}));  // open: dp
  LED led_1 (.in(out_11));
  LED led_2 (.in(out_10));
  LED led_3 (.in(out_9));
  meiocomp meiocomp_1 (
    .a(A0), .b(B0), .AmaiorqB(meiocomp_1_amaiorqb), .AigualqB(meiocomp_1_aigualqb),
    .AmenorqB(meiocomp_1_amenorqb));
  fullcomp fullcomp_1 (
    .a(A1), .b(B1), .Amaior_B(meiocomp_1_amaiorqb), .Aigual_B(meiocomp_1_aigualqb),
    .Amenor_B(meiocomp_1_amenorqb), .AmaiorqB(fullcomp_1_amaiorqb), .AigualqB(fullcomp_1_aigualqb),
    .AmenorqB(fullcomp_1_amenorqb));
  fullcomp fullcomp_2 (
    .a(A2), .b(B2), .Amaior_B(fullcomp_1_amaiorqb), .Aigual_B(fullcomp_1_aigualqb),
    .Amenor_B(fullcomp_1_amenorqb), .AmaiorqB(fullcomp_2_amaiorqb), .AigualqB(fullcomp_2_aigualqb),
    .AmenorqB(fullcomp_2_amenorqb));
  fullcomp fullcomp_3 (
    .a(A3), .b(B3), .Amaior_B(fullcomp_2_amaiorqb), .Aigual_B(fullcomp_2_aigualqb),
    .Amenor_B(fullcomp_2_amenorqb), .AmaiorqB(out_9), .AigualqB(out_10), .AmenorqB(out_11));
endmodule

module meiocomp (
  input  a,
  input  b,
  output AmaiorqB,
  output AigualqB,
  output AmenorqB
);

  wire and_2_out, and_3_out, not_1_out, not_2_out;

  not not_1 (not_1_out, a);
  not not_2 (not_2_out, b);
  and and_1 (AmaiorqB, a, not_2_out);
  and and_2 (and_2_out, not_1_out, not_2_out);
  and and_3 (and_3_out, a, b);
  and and_4 (AmenorqB, not_1_out, b);
  or or_1 (AigualqB, and_2_out, and_3_out);
endmodule

module fullcomp (
  input  a,
  input  b,
  input  Amaior_B,
  input  Aigual_B,
  input  Amenor_B,
  output AmaiorqB,
  output AigualqB,
  output AmenorqB
);

  wire and_1_out, and_2_out, and_3_out, and_4_out, and_5_out, and_6_out, and_7_out, and_8_out, and_9_out,
       and_10_out, not_1_out, not_2_out, not_3_out, not_4_out, not_5_out;

  not not_1 (not_1_out, a);
  not not_2 (not_2_out, b);
  not not_3 (not_3_out, Amaior_B);
  not not_4 (not_4_out, Aigual_B);
  not not_5 (not_5_out, Amenor_B);
  and and_1 (and_1_out, not_2_out, Amaior_B, not_4_out, not_5_out);
  and and_2 (and_2_out, a, not_2_out, not_3_out, not_4_out, Amenor_B);
  and and_3 (and_3_out, a, not_2_out, not_3_out, Aigual_B, not_5_out);
  and and_4 (and_4_out, a, Amaior_B, not_4_out, not_5_out);
  and and_5 (and_5_out, not_1_out, not_2_out, not_3_out, Aigual_B, not_5_out);
  and and_6 (and_6_out, a, b, not_3_out, Aigual_B, not_5_out);
  and and_7 (and_7_out, not_1_out, not_3_out, not_4_out, Amenor_B);
  and and_8 (and_8_out, b, not_3_out, not_4_out, Amenor_B);
  and and_9 (and_9_out, not_1_out, b, not_3_out, Aigual_B, not_5_out);
  and and_10 (and_10_out, not_1_out, b, Amaior_B, not_4_out, not_5_out);
  or or_1 (AmaiorqB, and_1_out, and_2_out, and_3_out, and_4_out);
  or or_2 (AigualqB, and_5_out, and_6_out);
  or or_3 (AmenorqB, and_7_out, and_8_out, and_9_out, and_10_out);
endmodule
