// Logisim project eeeeeetest.circ as structural Verilog: 6 circuits, main circuit main
module main (
  input  a1,
  input  b1,
  input  a2,
  input  b2,
  output igual,
  output amaior,
  output bmaior
);

  wire and_1_out, and_2_out, not_1_out, not_2_out, not_3_out, not_4_out, xor_1_out, xor_2_out;

  xor xor_1 (xor_1_out, a1, b1);
  xor xor_2 (xor_2_out, a2, b2);
  not not_1 (not_1_out, xor_1_out);
  not not_2 (not_2_out, xor_2_out);
  and and_1 (and_1_out, a1, not_3_out);
  not not_3 (not_3_out, b1);
  and and_2 (and_2_out, not_1_out, a2, not_4_out);
  not not_4 (not_4_out, b2);
  and and_3 (igual, not_1_out, not_2_out);
  or or_1 (amaior, and_1_out, and_2_out);
  nor nor_1 (bmaior, amaior, igual);
endmodule

module halfadder (
  input  a,
  input  b,
  output s,
  output te
);

  wire and_1_out, and_2_out, not_1_out, not_2_out;

  not not_1 (not_1_out, a);
  not not_2 (not_2_out, b);
  and and_1 (and_1_out, not_1_out, b);
  and and_2 (and_2_out, a, not_2_out);
  and and_3 (te, a, b);
  or or_1 (s, and_1_out, and_2_out);
endmodule

module fulladder (
  input  ts,
  input  a,
  input  b,
  output s,
  output te
);

  wire and_1_out, and_2_out, and_3_out, and_4_out, and_5_out, and_6_out, and_7_out, not_1_out, not_2_out,
       not_3_out;

  not not_1 (not_1_out, ts);
  not not_2 (not_2_out, a);
  not not_3 (not_3_out, b);
  and and_1 (and_1_out, not_1_out, not_2_out, b);
  and and_2 (and_2_out, not_1_out, a, not_3_out);
  and and_3 (and_3_out, ts, not_2_out, not_3_out);
  and and_4 (and_4_out, ts, a, b);
  and and_5 (and_5_out, a, b);
  and and_6 (and_6_out, ts, b);
  and and_7 (and_7_out, ts, a);
  or or_1 (s, and_1_out, and_2_out, and_3_out, and_4_out);
  or or_2 (te, and_5_out, and_6_out, and_7_out);
endmodule

module test (
  input  a,
  input  b,
  input  ts,
  output out_4,
  output out_5,
  output s,
  output te
);

  wire and_2_out, and_3_out, xor_1_out;

  xor xor_1 (xor_1_out, a, b);
  and and_1 (out_4, a, b);
  and and_2 (and_2_out, xor_1_out, ts);
  and and_3 (and_3_out, a, b);
  xor xor_2 (out_5, a, b);
  xor xor_3 (s, xor_1_out, ts);
  or or_1 (te, and_2_out, and_3_out);

  // Notes on the sheet:
  //   half adder
  //   full adder
  //   te
  //   s
endmodule

module halcomp (
  input  a,
  input  b,
  output AmaiorB,
  output AigualB,
  output AmenorB
);

  wire and_2_out, and_3_out, not_1_out, not_2_out;

  not not_1 (not_1_out, a);
  not not_2 (not_2_out, b);
  and and_1 (AmaiorB, a, not_2_out);
  and and_2 (and_2_out, not_1_out, not_2_out);
  and and_3 (and_3_out, a, b);
  and and_4 (AmenorB, not_1_out, b);
  or or_1 (AigualB, and_2_out, and_3_out);
endmodule

module fullcomp (
  input  a,
  input  b,
  input  AmaB,
  input  AigB,
  input  AmeB,
  output AmaiorB,
  output AigualB,
  output AmenorB
);

  wire and_1_out, and_2_out, and_3_out, and_4_out, and_5_out, and_6_out, and_7_out, and_8_out, and_9_out,
       and_10_out, not_1_out, not_2_out, not_3_out, not_4_out, not_5_out;

  not not_1 (not_1_out, a);
  not not_2 (not_2_out, b);
  not not_3 (not_3_out, AmaB);
  not not_4 (not_4_out, AigB);
  not not_5 (not_5_out, AmeB);
  and and_1 (and_1_out, not_2_out, AmaB, not_4_out, not_5_out);
  and and_2 (and_2_out, a, not_2_out, not_3_out, not_4_out, AmeB);
  and and_3 (and_3_out, a, not_2_out, not_3_out, AigB, not_5_out);
  and and_4 (and_4_out, a, AmaB, not_4_out, not_5_out);
  and and_5 (and_5_out, not_1_out, not_2_out, not_3_out, AigB, not_5_out);
  and and_6 (and_6_out, a, b, not_3_out, AigB, not_5_out);
  and and_7 (and_7_out, not_1_out, not_3_out, not_4_out, AmeB);
  and and_8 (and_8_out, b, not_3_out, not_4_out, AmeB);
  and and_9 (and_9_out, not_1_out, b, not_3_out, AigB, not_5_out);
  and and_10 (and_10_out, not_1_out, b, AmaB, not_4_out, not_5_out);
  or or_1 (AmaiorB, and_1_out, and_2_out, and_3_out, and_4_out);
  or or_2 (AigualB, and_5_out, and_6_out);
  or or_3 (AmenorB, and_7_out, and_8_out, and_9_out, and_10_out);
endmodule
