// Logisim project comparador.circ as structural Verilog: 3 circuits, main circuit main
module main (
  input  in_1,
  input  in_2,
  input  in_3,
  input  in_4,
  input  in_5,
  input  in_6,
  input  in_7,
  input  in_8
);

  wire fullcomp_1_aigualb, fullcomp_1_amaiorb, fullcomp_1_amenorb, fullcomp_2_aigualb, fullcomp_2_amaiorb,
       fullcomp_2_amenorb, fullcomp_3_aigualb, fullcomp_3_amaiorb, fullcomp_3_amenorb, halfcomp_1_aigualb,
       halfcomp_1_amaiorb, halfcomp_1_amenorb;

  HalfComp halfcomp_1 (
    .a(in_4), .b(in_8), .AmaiorB(halfcomp_1_amaiorb), .AigualB(halfcomp_1_aigualb),
    .AmenorB(halfcomp_1_amenorb));
  FullComp fullcomp_1 (
    .a(in_2), .b(in_6), .A_maiorB(fullcomp_2_amaiorb), .A_igualB(fullcomp_2_aigualb),
    .A_menorB(fullcomp_2_amenorb), .AmaiorB(fullcomp_1_amaiorb), .AigualB(fullcomp_1_aigualb),
    .AmenorB(fullcomp_1_amenorb));
  FullComp fullcomp_2 (
    .a(in_3), .b(in_7), .A_maiorB(halfcomp_1_amaiorb), .A_igualB(halfcomp_1_aigualb),
    .A_menorB(halfcomp_1_amenorb), .AmaiorB(fullcomp_2_amaiorb), .AigualB(fullcomp_2_aigualb),
    .AmenorB(fullcomp_2_amenorb));
  FullComp fullcomp_3 (
    .a(in_1), .b(in_5), .A_maiorB(fullcomp_1_amaiorb), .A_igualB(fullcomp_1_aigualb),
    .A_menorB(fullcomp_1_amenorb), .AmaiorB(fullcomp_3_amaiorb), .AigualB(fullcomp_3_aigualb),
    .AmenorB(fullcomp_3_amenorb));
  LED led_1 (.in(fullcomp_3_amaiorb));
  LED led_2 (.in(fullcomp_3_aigualb));
  LED led_3 (.in(fullcomp_3_amenorb));
  Hex_Digit_Display hex_digit_display_1 (.value({in_1, in_2, in_3, in_4}));  // open: dp
  Hex_Digit_Display hex_digit_display_2 (.value({in_5, in_6, in_7, in_8}));  // open: dp
endmodule

// HC
module HalfComp (
  input  a,
  input  b,
  output AmaiorB,
  output AigualB,
  output AmenorB
);

  wire and_2_out, and_3_out, not_1_out, not_2_out;

  not not_1 (not_1_out, a);
  not not_2 (not_2_out, b);
  and and_1 (AmaiorB, a, not_2_out);
  and and_2 (and_2_out, not_1_out, not_2_out);
  and and_3 (and_3_out, a, b);
  and and_4 (AmenorB, not_1_out, b);
  or or_1 (AigualB, and_2_out, and_3_out);
endmodule

// FC
module FullComp (
  input  a,
  input  b,
  input  A_maiorB,
  input  A_igualB,
  input  A_menorB,
  output AmaiorB,
  output AigualB,
  output AmenorB
);

  wire and_1_out, and_2_out, and_3_out, and_4_out, and_5_out, and_6_out, and_7_out, and_8_out, and_9_out,
       and_10_out, and_11_out, not_1_out, not_2_out, not_3_out, not_4_out, not_5_out;

  not not_1 (not_1_out, a);
  not not_2 (not_2_out, b);
  not not_3 (not_3_out, A_maiorB);
  not not_4 (not_4_out, A_igualB);
  not not_5 (not_5_out, A_menorB);
  and and_1 (and_1_out, not_2_out, A_maiorB, not_4_out, not_5_out);
  and and_2 (and_2_out, a, not_2_out, not_3_out, not_4_out, A_menorB);
  and and_3 (and_3_out, a, not_2_out, not_3_out, A_igualB, not_5_out);
  and and_4 (and_4_out, a, A_maiorB, not_4_out, not_5_out);
  and and_5 (and_5_out, not_1_out, not_2_out, not_3_out, A_igualB, not_5_out);
  and and_6 (and_6_out, a, b, not_3_out, A_igualB, not_5_out);
  and and_7 (and_7_out, a, b, A_maiorB, A_igualB, A_menorB);
  and and_8 (and_8_out, not_1_out, not_3_out, not_4_out, A_menorB);
  and and_9 (and_9_out, b, not_3_out, not_4_out, A_menorB);
  and and_10 (and_10_out, not_1_out, b, not_3_out, A_igualB, not_5_out);
  and and_11 (and_11_out, not_1_out, b, A_maiorB, not_4_out, not_5_out);
  or or_1 (AmaiorB, and_1_out, and_2_out, and_3_out, and_4_out);
  or or_2 (AigualB, and_5_out, and_6_out, and_7_out);
  or or_3 (AmenorB, and_8_out, and_9_out, and_10_out, and_11_out);
endmodule
