// Logisim project sobtrator.circ as structural Verilog: 3 circuits, main circuit main
module main (
  input  in_1,
  input  in_2,
  input  in_3,
  input  in_4,
  input  in_5,
  input  in_6,
  input  in_7,
  input  in_8,
  output out_9,
  output out_10,
  output out_11,
  output out_12,
  output out_13
);

  wire fullsubtractor_1_carry, fullsubtractor_2_carry, halfsubtractor_1_carry;

  halfSubtractor halfsubtractor_1 (.a(in_4), .b(in_8), .s(out_13), .carry(halfsubtractor_1_carry));
  fullSubtractor fullsubtractor_1 (
    .te(halfsubtractor_1_carry), .a(in_3), .b(in_7), .s(out_12), .carry(fullsubtractor_1_carry));
  fullSubtractor fullsubtractor_2 (
    .te(fullsubtractor_1_carry), .a(in_2), .b(in_6), .s(out_11), .carry(fullsubtractor_2_carry));
  fullSubtractor fullsubtractor_3 (.te(fullsubtractor_2_carry), .a(in_1), .b(in_5), .s(out_10), .carry(out_9));
  Hex_Digit_Display hex_digit_display_1 (.value({in_1, in_2, in_3, in_4}));  // open: dp
  Hex_Digit_Display hex_digit_display_2 (.value({3'b000, out_9}));  // open: dp
  Hex_Digit_Display hex_digit_display_3 (.value({in_5, in_6, in_7, in_8}));  // open: dp
  Hex_Digit_Display hex_digit_display_4 (.value({out_10, out_11, out_12, out_13}));  // open: dp
endmodule

// HS
module halfSubtractor (
  input  a,
  input  b,
  output s,
  output carry
);

  wire and_1_out, and_2_out, not_1_out, not_2_out;

  not not_1 (not_1_out, a);
  not not_2 (not_2_out, b);
  and and_1 (and_1_out, not_1_out, b);
  and and_2 (and_2_out, a, not_2_out);
  and and_3 (carry, not_1_out, b);
  or or_1 (s, and_1_out, and_2_out);
endmodule

// FS
module fullSubtractor (
  input  te,
  input  a,
  input  b,
  output s,
  output carry
);

  wire and_1_out, and_2_out, and_3_out, and_4_out, and_5_out, and_6_out, and_7_out, not_1_out, not_2_out,
       not_3_out;

  not not_1 (not_1_out, te);
  not not_2 (not_2_out, a);
  not not_3 (not_3_out, b);
  and and_1 (and_1_out, not_1_out, not_2_out, b);
  and and_2 (and_2_out, not_1_out, a, not_3_out);
  and and_3 (and_3_out, te, not_2_out, not_3_out);
  and and_4 (and_4_out, te, a, b);
  and and_5 (and_5_out, not_2_out, b);
  and and_6 (and_6_out, te, not_2_out);
  and and_7 (and_7_out, te, b);
  or or_1 (s, and_1_out, and_2_out, and_3_out, and_4_out);
  or or_2 (carry, and_5_out, and_6_out, and_7_out);
endmodule
