// Logisim project somador.circ as structural Verilog: 3 circuits, main circuit main
module main (
  input  in_1,
  input  in_2,
  input  in_3,
  input  in_4,
  input  in_5,
  input  in_6,
  input  in_7,
  input  in_8,
  output out_9,
  output out_10,
  output out_11,
  output out_12,
  output out_13
);

  wire fulladder_1_carry, fulladder_2_carry, halfadder_1_carry;

  halfAdder halfadder_1 (.a(in_4), .b(in_8), .s(out_13), .carry(halfadder_1_carry));
  fullAdder fulladder_1 (.te(halfadder_1_carry), .a(in_3), .b(in_7), .s(out_12), .carry(fulladder_1_carry));
  fullAdder fulladder_2 (.te(fulladder_1_carry), .a(in_2), .b(in_6), .s(out_11), .carry(fulladder_2_carry));
  fullAdder fulladder_3 (.te(fulladder_2_carry), .a(in_1), .b(in_5), .s(out_10), .carry(out_9));
  Hex_Digit_Display hex_digit_display_1 (.value({in_1, in_2, in_3, in_4}));  // open: dp
  Hex_Digit_Display hex_digit_display_2 (.value({in_5, in_6, in_7, in_8}));  // open: dp
  Hex_Digit_Display hex_digit_display_3 (.value({3'b000, out_9}));  // open: dp
  Hex_Digit_Display hex_digit_display_4 (.value({out_10, out_11, out_12, out_13}));  // open: dp
endmodule

// HA
module halfAdder (
  input  a,
  input  b,
  output s,
  output carry
);

  wire and_1_out, and_2_out, not_1_out, not_2_out;

  not not_1 (not_1_out, a);
  not not_2 (not_2_out, b);
  and and_1 (and_1_out, not_1_out, b);
  and and_2 (and_2_out, a, not_2_out);
  and and_3 (carry, a, b);
  or or_1 (s, and_1_out, and_2_out);
endmodule

// FA
module fullAdder (
  input  te,
  input  a,
  input  b,
  output s,
  output carry
);

  wire and_1_out, and_2_out, and_3_out, and_4_out, and_5_out, and_6_out, and_7_out, not_1_out, not_2_out,
       not_3_out;

  not not_1 (not_1_out, te);
  not not_2 (not_2_out, a);
  not not_3 (not_3_out, b);
  and and_1 (and_1_out, not_2_out, not_3_out, te);
  and and_2 (and_2_out, not_2_out, b, not_1_out);
  and and_3 (and_3_out, a, not_3_out, not_1_out);
  and and_4 (and_4_out, a, b, te);
  and and_5 (and_5_out, b, te);
  and and_6 (and_6_out, a, te);
  and and_7 (and_7_out, a, b);
  or or_1 (s, and_1_out, and_2_out, and_3_out, and_4_out);
  or or_2 (carry, and_5_out, and_6_out, and_7_out);
endmodule
