// Logisim project socorro.circ as structural Verilog
module main (
  input  in_1,
  input  in_2,
  input  in_3,
  input  in_4,
  input  in_5,
  output out_6
);

  wire xor_1_out, xor_2_out, xor_3_out, xor_4_out;

  xor xor_1 (xor_1_out, in_1, in_2);
  xor xor_2 (xor_2_out, xor_1_out, in_3);
  xor xor_3 (xor_3_out, xor_2_out, in_4);
  xor xor_4 (xor_4_out, xor_3_out, in_5);
  not not_1 (out_6, xor_4_out);
endmodule
